// Logisim project 1907121 CSE LAB 10.circ as structural Verilog: 1 circuit, main circuit main
module main (
  input  A,
  input  B,
  input  Ci,
  output S,
  output Co
);

  wire D1_out, D2_out, D3_out, D4_out, D5_out, D6_out, D7_out, not_1_out, not_2_out, not_3_out;

  not not_1 (not_1_out, A);
  not not_2 (not_2_out, B);
  not not_3 (not_3_out, Ci);
  // AND_Gate D0 has open pins: in0=not_1_out, in1=not_2_out, in2=not_3_out, out=open
  and D1 (D1_out, not_1_out, not_2_out, Ci);
  and D2 (D2_out, not_1_out, B, not_3_out);
  and D3 (D3_out, not_1_out, B, Ci);
  and D4 (D4_out, A, not_2_out, not_3_out);
  and D5 (D5_out, A, not_2_out, Ci);
  and D6 (D6_out, A, B, not_3_out);
  and D7 (D7_out, A, B, Ci);
  or or_1 (S, D1_out, D2_out, D4_out, D7_out);
  or or_2 (Co, D3_out, D5_out, D6_out, D7_out);
endmodule
