// Logisim project 1907121 CSE 11(BASIC).circ as structural Verilog: 1 circuit, main circuit main
module main (
  input  X,
  output Qa,
  output Y,
  output Qb,
  output Qc
);

  wire and_1_out, and_2_out, and_3_out, and_4_out, and_5_out, CLK_out, not_1_out, not_2_out, not_3_out,
       not_4_out, not_5_out, not_6_out, not_7_out, or_1_out, or_2_out, or_3_out, QaQc_out, Qb_prime_X_out,
       QbQc_out, QbQc_prime_out;

  Clock CLK (.out(CLK_out));
  not not_1 (not_1_out, X);
  not not_2 (not_2_out, Qb);
  not not_3 (not_3_out, Qc);
  not not_4 (not_4_out, Qc);
  and Qb_prime_X (Qb_prime_X_out, X, not_2_out);
  and QbQc (QbQc_out, Qb, Qc);
  and QaQc (QaQc_out, Qc, Qa);
  and QbQc_prime (QbQc_prime_out, Qb, not_3_out);
  and and_1 (and_1_out, Qa, not_3_out, not_1_out);
  and and_2 (and_2_out, not_1_out, not_2_out, Qc, not_5_out);
  not not_5 (not_5_out, Qa);
  and and_3 (and_3_out, not_5_out, not_2_out, not_4_out);
  or or_1 (or_1_out, Qb_prime_X_out, QbQc_out, QaQc_out);
  or or_2 (or_2_out, QbQc_prime_out, and_1_out, and_2_out);
  or or_3 (or_3_out, and_3_out, X);
  D_Flip_Flop A (.clk(CLK_out), .D(or_1_out), .Q(Qa));  // open: Qn, preset, en, reset
  D_Flip_Flop B (.clk(CLK_out), .D(or_2_out), .Q(Qb));  // open: Qn, preset, en, reset
  D_Flip_Flop C (.clk(CLK_out), .D(or_3_out), .Q(Qc));  // open: Qn, preset, en, reset
  not not_6 (not_6_out, X);
  not not_7 (not_7_out, Qc);
  and and_4 (and_4_out, not_6_out, Qb, Qc);
  and and_5 (and_5_out, not_6_out, Qa, not_7_out);
  or or_4 (Y, and_4_out, and_5_out);
endmodule
