// Logisim project 1907121 CSE 11(NAND).circ as structural Verilog: 1 circuit, main circuit main
module main (
  input  X,
  output Y
);

  wire clock_1_out, d_ff_1_q, d_ff_2_q, d_ff_3_q, nand_1_out, nand_2_out, nand_3_out, nand_5_out, not_1_out,
       not_2_out, not_3_out, not_4_out, not_5_out, Qa_prime_Qb_prime_Qc_prime__prime_out,
       Qa_prime_Qb_prime_QcX_prime__prime_out, QaQc_prime_X_prime__prime_out, Qb_prime_X__prime_out,
       QbQc__prime_2_out, QbQc__prime_out, QbQc_prime__prime_out;

  Clock clock_1 (.out(clock_1_out));
  nand nand_1 (nand_1_out, Qb_prime_X__prime_out, QbQc__prime_2_out, QbQc__prime_out);
  nand Qb_prime_X__prime (Qb_prime_X__prime_out, X, not_4_out);
  D_Flip_Flop d_ff_1 (.clk(clock_1_out), .D(nand_1_out), .Q(d_ff_1_q));  // open: Qn, preset, en, reset
  nand QbQc__prime (QbQc__prime_out, X, d_ff_3_q);
  nand QbQc__prime_2 (QbQc__prime_2_out, d_ff_3_q, d_ff_1_q);
  not not_1 (not_1_out, d_ff_1_q);
  not not_2 (not_2_out, X);
  nand Qa_prime_Qb_prime_QcX_prime__prime (Qa_prime_Qb_prime_QcX_prime__prime_out, not_2_out, not_1_out, not_4_out, d_ff_3_q);
  nand nand_2 (nand_2_out, d_ff_3_q, d_ff_2_q, not_2_out);
  nand nand_3 (nand_3_out, Qa_prime_Qb_prime_QcX_prime__prime_out, QaQc_prime_X_prime__prime_out, QbQc_prime__prime_out);
  nand QaQc_prime_X_prime__prime (QaQc_prime_X_prime__prime_out, d_ff_1_q, not_2_out, not_3_out);
  not not_3 (not_3_out, d_ff_3_q);
  not not_4 (not_4_out, d_ff_2_q);
  D_Flip_Flop d_ff_2 (.clk(clock_1_out), .D(nand_3_out), .Q(d_ff_2_q));  // open: Qn, preset, en, reset
  nand QbQc_prime__prime (QbQc_prime__prime_out, not_3_out, d_ff_2_q);
  not not_5 (not_5_out, X);
  nand nand_4 (Y, QaQc_prime_X_prime__prime_out, nand_2_out);
  nand nand_5 (nand_5_out, not_5_out, Qa_prime_Qb_prime_Qc_prime__prime_out);
  nand Qa_prime_Qb_prime_Qc_prime__prime (Qa_prime_Qb_prime_Qc_prime__prime_out, not_1_out, not_4_out, not_3_out);
  D_Flip_Flop d_ff_3 (.clk(clock_1_out), .D(nand_5_out), .Q(d_ff_3_q));  // open: Qn, preset, en, reset
endmodule
