// Logisim project 1907121 Lab Task 1.circ as structural Verilog
module NAND (
  input  a,
  input  b,
  output \nand 
);

  wire and_1_out;

  and and_1 (and_1_out, a, b);
  not not_1 (\nand , and_1_out);

  // Notes on the sheet:
  //   NAND GATE
  //   Output = ~(a b)
endmodule

module NOR (
  input  a,
  input  b,
  output \nor 
);

  wire or_1_out;

  or or_1 (or_1_out, a, b);
  not not_1 (\nor , or_1_out);

  // Notes on the sheet:
  //   NOR GATE
  //   Output = ~(a+b)
endmodule

module AND (
  input  a,
  input  b,
  output \and 
);

  and and_1 (\and , a, b);

  // Notes on the sheet:
  //   AND GATE
  //   Output = a b
endmodule

module OR (
  input  a,
  input  b,
  output \or 
);

  or or_1 (\or , a, b);

  // Notes on the sheet:
  //   OR GATE
  //   Output = a+b
endmodule

module NOT (
  input  a,
  output \not 
);

  not not_1 (\not , a);

  // Notes on the sheet:
  //   NOT GATE
  //   Output = ~a
endmodule

module EX_OR (
  input  a,
  input  b,
  input  a_2,
  input  b_2,
  output EX_OR,
  output c
);

  wire and_1_out, and_2_out, not_1_out, not_2_out;

  not not_1 (not_1_out, a);
  not not_2 (not_2_out, b);
  and and_1 (and_1_out, a, not_2_out);
  and and_2 (and_2_out, not_1_out, b, b);
  xor xor_1 (c, a_2, b_2);
  or or_1 (EX_OR, and_1_out, and_2_out);

  // Notes on the sheet:
  //   X-OR GATE
  //   ab'
  //   a'b
  //   Output = ab' + a'b
  //   Output = ab' + a'b
endmodule

module EX_NOR (
  input  a,
  input  b,
  output EX_NOR
);

  wire and_1_out, and_2_out, not_1_out, not_2_out;

  not not_1 (not_1_out, a);
  not not_2 (not_2_out, b);
  and and_1 (and_1_out, a, b);
  and and_2 (and_2_out, not_1_out, not_2_out, not_2_out);
  or or_1 (EX_NOR, and_1_out, and_2_out);

  // Notes on the sheet:
  //   X-NOR GATE
  //   ab
  //   a'b'
  //   Output = ab + a'b'
endmodule

module X_NOR_using_NAND (
  input  A,
  input  B,
  output C
);

  wire NAND_2_out, NAND_3_out, NAND_4_out, NAND_out;

  nand NAND (NAND_out, A, A);
  nand NAND_2 (NAND_2_out, B, B);
  nand NAND_3 (NAND_3_out, A, B);
  nand NAND_4 (NAND_4_out, NAND_out, NAND_2_out);
  nand NAND_5 (C, NAND_4_out, NAND_3_out, NAND_3_out);
endmodule
