// Logisim project 1907121 lab 2.circ as structural Verilog
module WITH_NOR (
  input  A,
  input  B,
  input  C,
  input  D,
  output Y
);

  wire nor_1_out, nor_2_out, nor_3_out, nor_4_out, nor_5_out, nor_6_out, nor_7_out, nor_8_out, nor_9_out;

  nor nor_1 (nor_1_out, A, A);
  nor nor_2 (nor_2_out, B, B);
  nor nor_3 (nor_3_out, C, C);
  nor nor_4 (nor_4_out, D, D);
  nor nor_5 (nor_5_out, A, nor_4_out, nor_3_out);
  nor nor_6 (nor_6_out, nor_1_out, B, D);
  nor nor_7 (nor_7_out, nor_2_out, nor_4_out);
  nor nor_8 (nor_8_out, D, D, C, B);
  nor nor_9 (nor_9_out, nor_5_out, nor_6_out, nor_7_out, nor_8_out);
  nor nor_10 (Y, nor_9_out, nor_9_out);

  // Notes on the sheet:
  //   4
  //   1
endmodule

module WITH_NAND (
  input  A,
  input  B,
  input  C,
  input  D,
  output Y
);

  wire nand_1_out, nand_2_out, nand_3_out, nand_4_out, nand_5_out, nand_6_out, nand_7_out, nand_8_out;

  nand nand_1 (nand_1_out, A, A);
  nand nand_2 (nand_2_out, B, B);
  nand nand_3 (nand_3_out, C, C);
  nand nand_4 (nand_4_out, D, D);
  nand nand_5 (nand_5_out, A, nand_2_out, nand_4_out);
  nand nand_6 (nand_6_out, B, D);
  nand nand_7 (nand_7_out, nand_2_out, nand_3_out, nand_4_out);
  nand nand_8 (nand_8_out, D, C, nand_1_out);
  nand nand_9 (Y, nand_8_out, nand_5_out, nand_6_out, nand_7_out);

  // Notes on the sheet:
  //   3
  //   1
  //   2
endmodule

module COMMON_GATE (
  input  A,
  input  B,
  input  C,
  input  D,
  output Y
);

  wire and_1_out, and_2_out, and_3_out, and_4_out, not_1_out, not_2_out, not_3_out, not_4_out;

  not not_1 (not_1_out, A);
  not not_2 (not_2_out, B);
  not not_3 (not_3_out, C);
  not not_4 (not_4_out, D);
  and and_1 (and_1_out, B, B, D);
  and and_2 (and_2_out, not_2_out, not_3_out, not_4_out);
  and and_3 (and_3_out, A, not_2_out, not_4_out);
  and and_4 (and_4_out, not_1_out, C, D);
  or or_1 (Y, and_3_out, and_4_out, and_1_out, and_2_out);
endmodule
