// Logisim project 1907121 CSE LAB 3 Task.circ as structural Verilog
module Half_Adder (
  input  A,
  input  B,
  output S,
  output C
);

  xor xor_1 (S, A, B);
  and and_1 (C, A, B);
endmodule

module Full_Adder (
  input  A,
  input  B,
  input  Cin,
  output S,
  output Co
);

  wire and_1_out, and_2_out, xor_1_out;

  xor xor_1 (xor_1_out, A, B);
  and and_1 (and_1_out, A, B);
  xor xor_2 (S, xor_1_out, Cin);
  and and_2 (and_2_out, xor_1_out, Cin);
  or or_1 (Co, and_2_out, and_1_out);
endmodule

module Half_Substractor (
  input  A,
  input  B,
  output D,
  output Bo
);

  wire not_1_out;

  not not_1 (not_1_out, A);
  xor xor_1 (D, A, B);
  and and_1 (Bo, B, not_1_out);
endmodule

module Full_Substractor (
  input  A,
  input  B,
  input  Cin,
  output D,
  output Bo
);

  wire and_1_out, and_2_out, not_1_out, not_2_out, xor_1_out;

  not not_1 (not_1_out, A);
  xor xor_1 (xor_1_out, A, B);
  and and_1 (and_1_out, not_1_out, B);
  xor xor_2 (D, xor_1_out, Cin);
  not not_2 (not_2_out, xor_1_out);
  and and_2 (and_2_out, not_2_out, Cin);
  or or_1 (Bo, and_2_out, and_1_out);
endmodule
