// Logisim project 1907121 CSE LAB-04.circ as structural Verilog
module Binary_to_Gray_using_NOR (
  input  B3,
  input  B2,
  input  B1,
  input  B0,
  output G3,
  output G2,
  output G1,
  output G0
);

  wire nor_1_out, nor_2_out, nor_3_out, nor_4_out, nor_5_out, nor_6_out, nor_7_out, nor_8_out, nor_9_out,
       nor_10_out, nor_11_out, nor_12_out, nor_13_out;

  nor nor_1 (nor_1_out, B3, B3);
  nor nor_2 (nor_2_out, B2, B2);
  nor nor_3 (nor_3_out, B1, B1);
  nor nor_4 (nor_4_out, B0, B0);
  nor nor_5 (nor_5_out, B3, nor_2_out);
  nor nor_6 (nor_6_out, nor_1_out, B2);
  nor nor_7 (nor_7_out, B2, nor_3_out);
  nor nor_8 (nor_8_out, nor_2_out, B1);
  nor nor_9 (nor_9_out, B1, nor_4_out);
  nor nor_10 (nor_10_out, nor_3_out, B0);
  nor nor_11 (nor_11_out, nor_5_out, nor_6_out);
  nor nor_12 (nor_12_out, nor_7_out, nor_8_out);
  nor nor_13 (nor_13_out, nor_9_out, nor_10_out);
  nor nor_14 (G2, nor_11_out, nor_11_out);
  nor nor_15 (G1, nor_12_out, nor_12_out);
  nor nor_16 (G0, nor_13_out, nor_13_out);

  assign G3 = B3;
endmodule

module Gray_to_Binary_using_NOR (
  input  G3,
  input  G2,
  input  G,
  input  G0,
  output B3,
  output B2,
  output B1,
  output B0
);

  wire nor_1_out, nor_2_out, nor_3_out, nor_4_out, nor_5_out, nor_6_out, nor_7_out, nor_8_out, nor_9_out,
       nor_10_out, nor_11_out, nor_12_out;

  nor nor_1 (nor_1_out, G3, G2);
  nor nor_2 (nor_2_out, B2, G);
  nor nor_3 (nor_3_out, B1, G0);
  nor nor_4 (nor_4_out, G3, nor_1_out);
  nor nor_5 (nor_5_out, nor_1_out, G2);
  nor nor_6 (nor_6_out, B2, nor_2_out);
  nor nor_7 (nor_7_out, nor_2_out, G);
  nor nor_8 (nor_8_out, B1, nor_3_out);
  nor nor_9 (nor_9_out, nor_3_out, G0);
  nor nor_10 (nor_10_out, nor_4_out, nor_5_out);
  nor nor_11 (nor_11_out, nor_6_out, nor_7_out);
  nor nor_12 (nor_12_out, nor_8_out, nor_9_out);
  nor nor_13 (B2, nor_10_out, nor_10_out);
  nor nor_14 (B1, nor_11_out, nor_11_out);
  nor nor_15 (B0, nor_12_out, nor_12_out);

  assign B3 = G3;
endmodule
