// Logisim project 1907121 CSE LAB 07 SR.circ as structural Verilog: 1 circuit, main circuit main
module main (
  input  S,
  input  R,
  output Q,
  output Qb
);

  wire CLK_out, nand_1_out, nand_2_out;

  Clock CLK (.out(CLK_out));
  nand nand_1 (nand_1_out, S, CLK_out);
  nand nand_2 (nand_2_out, CLK_out, R);
  nand nand_3 (Q, nand_1_out, Qb);
  nand nand_4 (Qb, Q, nand_2_out);
endmodule
