// Logisim project 1907121 CSE LAB Task 8 ultimate.circ as structural Verilog: 1 circuit, main circuit main
module main (
  output q4,
  output q3,
  output q2,
  output q1
);

  wire clock_1_out, q2q1_out;

  Clock clock_1 (.out(clock_1_out));
  J_K_Flip_Flop _1 (.J(q4), .clk(clock_1_out), .K(1'b1), .Q(q1));  // open: Qn, preset, en, reset
  J_K_Flip_Flop _2 (.J(q1), .clk(clock_1_out), .K(q1), .Q(q2));  // open: Qn, preset, en, reset
  and q2q1 (q2q1_out, q2, q1);
  J_K_Flip_Flop _3 (.J(q4), .clk(clock_1_out), .K(q2q1_out), .Q(q3));  // open: Qn, preset, en, reset
  J_K_Flip_Flop _4 (.J(1'b1), .clk(clock_1_out), .K(q2q1_out), .Q(q4));  // open: Qn, preset, en, reset
endmodule
