// Logisim project 1907121 CSE LAB 08.circ as structural Verilog: 1 circuit, main circuit main
module main (
  input  Q1,
  input  Q2,
  input  Q3,
  input  Q4
);

  wire and_1_out, clock_1_out, JK1_q, JK2_q, JK3_q, JK4_q;

  Clock clock_1 (.out(clock_1_out));
  J_K_Flip_Flop JK1 (.J(Q4), .clk(clock_1_out), .K(1'b1), .Q(JK1_q));  // open: Qn, preset, en, reset
  and and_1 (and_1_out, Q1, Q2);
  J_K_Flip_Flop JK2 (.J(Q1), .clk(clock_1_out), .K(Q1), .Q(JK2_q));  // open: Qn, preset, en, reset
  J_K_Flip_Flop JK3 (.J(Q4), .clk(clock_1_out), .K(and_1_out), .Q(JK3_q));  // open: Qn, preset, en, reset
  J_K_Flip_Flop JK4 (.J(1'b1), .clk(clock_1_out), .K(and_1_out), .Q(JK4_q));  // open: Qn, preset, en, reset
endmodule
