// Logisim project 1907121 CSE LAB 09 (15-3 down).circ as structural Verilog: 1 circuit, main circuit main
module main (
  output out_1,
  output out_2,
  output out_3,
  output out_4
);

  wire and_1_out, clock_1_out, nor_1_out, t_ff_1_qn, t_ff_2_qn, t_ff_3_qn;

  Clock clock_1 (.out(clock_1_out));
  T_Flip_Flop #(.trigger("falling")) t_ff_1 (
    .clk(clock_1_out), .T(1'b1), .Q(out_4), .Qn(t_ff_1_qn), .preset(and_1_out), .en(1'b1));  // open: reset
  T_Flip_Flop #(.trigger("falling")) t_ff_2 (
    .clk(t_ff_1_qn), .T(1'b1), .Q(out_3), .Qn(t_ff_2_qn), .preset(and_1_out), .en(1'b1));  // open: reset
  T_Flip_Flop #(.trigger("falling")) t_ff_3 (
    .clk(t_ff_2_qn), .T(1'b1), .Q(out_2), .Qn(t_ff_3_qn), .preset(and_1_out), .en(1'b1));  // open: reset
  T_Flip_Flop #(.trigger("falling")) t_ff_4 (
    .clk(t_ff_3_qn), .T(1'b1), .Q(out_1), .preset(and_1_out), .en(1'b1));  // open: Qn, reset
  nor nor_1 (nor_1_out, out_1, out_4, out_2);
  and and_1 (and_1_out, nor_1_out, out_3);

  // Notes on the sheet:
  //   Negative Clock Pulse Trigger
  //   Fig: 4 BIT Asynchronous Down Counter
endmodule
