// Logisim project 1907121 CSE LAB 09 up and down.circ as structural Verilog: 1 circuit, main circuit main
module main (
  output out_1,
  output out_2,
  output out_3,
  output out_4,
  output out_5,
  output out_6,
  output out_7,
  output out_8
);

  wire clock_1_out, clock_2_out, not_1_out, not_2_out, t_ff_1_qn, t_ff_2_qn, t_ff_3_qn, t_ff_4_qn, t_ff_5_qn,
       t_ff_6_qn;

  Clock clock_1 (.out(clock_1_out));
  Clock clock_2 (.out(clock_2_out));
  T_Flip_Flop t_ff_1 (
    .clk(clock_1_out), .T(1'b1), .Q(out_4), .Qn(t_ff_1_qn), .reset(not_1_out), .en(1'b1));  // open: preset
  T_Flip_Flop #(.trigger("falling")) t_ff_2 (
    .clk(clock_2_out), .T(1'b1), .Q(out_8), .Qn(t_ff_2_qn), .reset(not_2_out), .en(1'b1));  // open: preset
  not not_1 (not_1_out, 1'b1);
  not not_2 (not_2_out, 1'b1);
  T_Flip_Flop t_ff_3 (
    .clk(t_ff_1_qn), .T(1'b1), .Q(out_3), .Qn(t_ff_3_qn), .reset(not_1_out), .en(1'b1));  // open: preset
  T_Flip_Flop #(.trigger("falling")) t_ff_4 (
    .clk(t_ff_2_qn), .T(1'b1), .Q(out_7), .Qn(t_ff_4_qn), .reset(not_2_out), .en(1'b1));  // open: preset
  T_Flip_Flop #(.trigger("falling")) t_ff_5 (
    .clk(t_ff_4_qn), .T(1'b1), .Q(out_6), .Qn(t_ff_5_qn), .en(1'b1));  // open: preset, reset
  T_Flip_Flop t_ff_6 (.clk(t_ff_3_qn), .T(1'b1), .Q(out_2), .Qn(t_ff_6_qn), .en(1'b1));  // open: preset, reset
  T_Flip_Flop t_ff_7 (.clk(t_ff_6_qn), .T(1'b1), .Q(out_1), .en(1'b1));  // open: Qn, preset, reset
  T_Flip_Flop #(.trigger("falling")) t_ff_8 (
    .clk(t_ff_5_qn), .T(1'b1), .Q(out_5), .en(1'b1));  // open: Qn, preset, reset

  // Notes on the sheet:
  //   Positive Clock Pulse Trigger
  //   Negative Clock Pulse Trigger
  //   Fig: 4 BIT Asynchronous Up Counter
  //   Fig: 4 BIT Asynchronous Down Counter
endmodule
