// Logisim project 1907121 CSE LAB 09(down 15-3).circ as structural Verilog: 1 circuit, main circuit main
module main (
  output out_1,
  output out_2,
  output out_3,
  output out_4
);

  wire and_1_out, clock_1_out, not_1_out, not_2_out, not_3_out;

  Clock clock_1 (.out(clock_1_out));
  J_K_Flip_Flop j_k_ff_1 (.J(1'b1), .clk(clock_1_out), .K(1'b1), .Q(out_4), .reset(and_1_out));  // open: Qn, preset, en
  not not_1 (not_1_out, out_4);
  J_K_Flip_Flop j_k_ff_2 (.J(1'b1), .clk(out_4), .K(1'b1), .Q(out_3), .reset(and_1_out));  // open: Qn, preset, en
  J_K_Flip_Flop j_k_ff_3 (.J(1'b1), .clk(out_3), .K(1'b1), .Q(out_2), .reset(and_1_out));  // open: Qn, preset, en
  not not_2 (not_2_out, out_2);
  J_K_Flip_Flop j_k_ff_4 (.J(1'b1), .clk(out_2), .K(1'b1), .Q(out_1), .reset(and_1_out));  // open: Qn, preset, en
  not not_3 (not_3_out, out_1);
  and and_1 (and_1_out, not_3_out, not_2_out, out_3, not_1_out);
endmodule
