// Logisim project 1907121 CSE LAB 09(up 0-12).circ as structural Verilog: 1 circuit, main circuit main
module main (
  output out_1,
  output out_2,
  output out_3,
  output out_4
);

  wire and_1_out, clock_1_out;

  Clock clock_1 (.out(clock_1_out));
  J_K_Flip_Flop #(.trigger("falling")) j_k_ff_1 (
    .J(1'b1), .clk(clock_1_out), .K(1'b1), .Q(out_4), .reset(and_1_out));  // open: Qn, preset, en
  J_K_Flip_Flop #(.trigger("falling")) j_k_ff_2 (
    .J(1'b1), .clk(out_4), .K(1'b1), .Q(out_3), .reset(and_1_out));  // open: Qn, preset, en
  J_K_Flip_Flop #(.trigger("falling")) j_k_ff_3 (
    .J(1'b1), .clk(out_3), .K(1'b1), .Q(out_2), .reset(and_1_out));  // open: Qn, preset, en
  J_K_Flip_Flop #(.trigger("falling")) j_k_ff_4 (
    .J(1'b1), .clk(out_2), .K(1'b1), .Q(out_1), .reset(and_1_out));  // open: Qn, preset, en
  and and_1 (and_1_out, out_4, out_2, out_1);
endmodule
