// Logisim project 1907121 lab 9.circ as structural Verilog: 1 circuit, main circuit main
module main (
);

  wire clock_1_out, j_k_ff_1_q, j_k_ff_2_q, j_k_ff_3_q, j_k_ff_4_q, not_1_out, not_2_out, not_3_out,
       not_4_out, not_5_out, not_6_out, not_7_out, not_8_out, not_9_out, not_10_out, not_11_out, not_12_out;

  Clock clock_1 (.out(clock_1_out));
  not not_1 (not_1_out, clock_1_out);
  J_K_Flip_Flop j_k_ff_1 (
    .clk(not_1_out), .Q(j_k_ff_1_q), .preset(not_2_out), .en(not_3_out), .reset(not_3_out));  // open: J, K, Qn
  not not_2 (not_2_out, 1'b1);
  // NOT_Gate not_3 has open pins: in=open, out=not_3_out
  not not_4 (not_4_out, j_k_ff_1_q);
  not not_5 (not_5_out, 1'b1);
  // NOT_Gate not_6 has open pins: in=open, out=not_6_out
  J_K_Flip_Flop j_k_ff_2 (
    .clk(not_4_out), .Q(j_k_ff_2_q), .preset(not_5_out), .reset(not_6_out));  // open: J, K, Qn, en
  not not_7 (not_7_out, j_k_ff_2_q);
  J_K_Flip_Flop j_k_ff_3 (
    .clk(not_7_out), .Q(j_k_ff_3_q), .preset(not_8_out), .reset(not_9_out));  // open: J, K, Qn, en
  not not_8 (not_8_out, 1'b1);
  // NOT_Gate not_9 has open pins: in=open, out=not_9_out
  J_K_Flip_Flop j_k_ff_4 (
    .clk(not_10_out), .Q(j_k_ff_4_q), .preset(not_11_out), .reset(not_12_out));  // open: J, K, Qn, en
  not not_10 (not_10_out, j_k_ff_3_q);
  not not_11 (not_11_out, 1'b1);
  // NOT_Gate not_12 has open pins: in=open, out=not_12_out
endmodule
