// Logisim project 1.Not Gate.circ as structural Verilog: 1 circuit, main circuit main
module main (
  input  in_1,
  output out_2
);

  not not_1 (out_2, in_1);

  // Notes on the sheet:
  //   !at Operation
  //   NOT Gate
endmodule
