// Logisim project 4.NOR Gate.circ as structural Verilog: 1 circuit, main circuit main
module main (
  input  in_1,
  input  in_2,
  input  A,
  input  B,
  input  A_2,
  input  B_2,
  output out_7,
  output out_8,
  output out_9
);

  wire not_1_out, not_2_out, or_1_out;

  nor nor_1 (out_7, in_1, in_2);
  or or_1 (or_1_out, A, B);
  not not_1 (not_1_out, A_2);
  not not_2 (not_2_out, B_2);
  not not_3 (out_8, or_1_out);
  and and_1 (out_9, not_1_out, not_2_out);

  // Notes on the sheet:
  //   NOR Gate
endmodule
