// Logisim project 5.X-OR Gate.circ as structural Verilog: 1 circuit, main circuit main
module main (
  input  in_1,
  input  in_2,
  input  A,
  input  B,
  input  a_2,
  input  b_2,
  output out_7,
  output out_8,
  output \xor 
);

  wire and_1_out, and_2_out, and_3_out, and_4_out, not_1_out, not_2_out, not_3_out, not_4_out;

  xor xor_1 (out_7, in_1, in_2);
  not not_1 (not_1_out, A);
  not not_2 (not_2_out, B);
  not not_3 (not_3_out, a_2);
  not not_4 (not_4_out, b_2);
  and and_1 (and_1_out, A, not_2_out);
  and and_2 (and_2_out, not_1_out, B, B);
  and and_3 (and_3_out, not_4_out, a_2, a_2);
  and and_4 (and_4_out, not_3_out, b_2);
  or or_1 (out_8, and_1_out, and_2_out);
  or or_2 (\xor , and_3_out, and_4_out);

  // Notes on the sheet:
  //   a'
  //   b'
  //   ab'
  //   a'b
  //   X-OR Gate
endmodule
