// Logisim project 6.X-NOR Gate.circ as structural Verilog: 1 circuit, main circuit main
module main (
  input  in_1,
  input  in_2,
  input  A,
  input  B,
  input  A_2,
  input  B_2,
  output out_7,
  output out_8,
  output out_9
);

  wire and_1_out, and_2_out, and_3_out, and_4_out, not_1_out, not_2_out, not_3_out, not_4_out, or_1_out;

  not not_1 (not_1_out, A);
  not not_2 (not_2_out, B);
  not not_3 (not_3_out, B_2);
  not not_4 (not_4_out, A_2);
  xnor xnor_1 (out_7, in_1, in_2);
  and and_1 (and_1_out, A, B);
  and and_2 (and_2_out, not_1_out, not_2_out);
  and and_3 (and_3_out, A_2, not_3_out);
  and and_4 (and_4_out, not_4_out, B_2);
  or or_1 (or_1_out, and_3_out, and_4_out);
  or or_2 (out_8, and_1_out, and_2_out);
  not not_5 (out_9, or_1_out);

  // Notes on the sheet:
  //   X-NOR Gate
endmodule
