// Logisim project Lab Class 1 Gate.circ as structural Verilog: 2 circuits, main circuit main
// a
module main (
  input  a,
  input  b,
  output \output 
);

  NAND nand_1 (.x(a), .y(b), .\nand (\output ));
endmodule

module NAND (
  input  x,
  input  y,
  output \nand 
);

  wire and_1_out;

  and and_1 (and_1_out, x, x, y);
  not not_1 (\nand , and_1_out);
endmodule
