// Logisim project hashem sir hw.circ as structural Verilog: 1 circuit, main circuit main
module main (
  input  x,
  output out_2,
  output out_3,
  output out_4,
  output \output 
);

  wire A_qn, B_qn, C_qn, clock_1_out, nand_1_out, nand_2_out, nand_3_out, nand_4_out, nand_5_out, nand_6_out,
       nand_7_out, nand_8_out, nand_9_out, nand_10_out, nand_11_out, nand_12_out, nand_13_out;

  not nand_1 (nand_1_out, x);  // NAND_Gate
  Clock clock_1 (.out(clock_1_out));
  nand nand_2 (nand_2_out, out_2, out_4);
  nand nand_3 (nand_3_out, out_4, out_3);
  nand nand_4 (nand_4_out, x, B_qn);
  nand nand_5 (nand_5_out, out_3, C_qn);
  nand nand_6 (nand_6_out, C_qn, nand_1_out, out_2);
  nand nand_7 (nand_7_out, out_4, B_qn, A_qn, nand_1_out);
  nand nand_8 (nand_8_out, A_qn, B_qn, C_qn);
  nand nand_9 (nand_9_out, nand_2_out, nand_3_out, nand_4_out);
  nand nand_10 (nand_10_out, nand_5_out, nand_6_out, nand_7_out);
  nand nand_11 (nand_11_out, nand_8_out, nand_1_out);
  D_Flip_Flop A (.clk(clock_1_out), .D(nand_9_out), .Q(out_2), .Qn(A_qn));  // open: preset, en, reset
  D_Flip_Flop B (.clk(clock_1_out), .D(nand_10_out), .Q(out_3), .Qn(B_qn));  // open: preset, en, reset
  D_Flip_Flop C (.clk(clock_1_out), .D(nand_11_out), .Q(out_4), .Qn(C_qn));  // open: preset, en, reset
  nand nand_12 (nand_12_out, out_3, out_4, nand_1_out);
  nand nand_13 (nand_13_out, out_2, C_qn, nand_1_out);
  nand nand_14 (\output , nand_12_out, nand_13_out);
endmodule
