// Logisim project jkahsjhs.circ as structural Verilog: 1 circuit, main circuit main
module main (
  input  Q4,
  input  Q3,
  input  Q2,
  input  Q1,
  input  in_5
);

  wire and_1_out, clock_1_out;

  and and_1 (and_1_out, Q2, Q1);
  Clock clock_1 (.out(clock_1_out));
  J_K_Flip_Flop JK4 (.J(in_5), .clk(clock_1_out), .K(and_1_out), .Q(Q4));  // open: Qn, preset, en, reset
  J_K_Flip_Flop JK3 (.J(Q4), .clk(clock_1_out), .K(and_1_out), .Q(Q3));  // open: Qn, preset, en, reset
  J_K_Flip_Flop JK2 (.J(Q1), .clk(clock_1_out), .K(Q1), .Q(Q2));  // open: Qn, preset, en, reset
  J_K_Flip_Flop JK1 (.J(Q4), .clk(clock_1_out), .K(in_5), .Q(Q1));  // open: Qn, preset, en, reset
endmodule
